# Fritzing sketch schematic (saved by Fritzing 0.9.2b)

parts:
  step_down_converter = IC, DIP package, 4 pins
  arduino_nano = Arduino Nano (Rev3.0)
  part = Resistor [tolerance=±5% resistance=4.7k package=THT]
  part_2 = Resistor [tolerance=±5% resistance=2.2k package=THT]
  part_3 = Resistor [tolerance=±5% resistance=2.2k package=THT]
  MCP2003B = IC, DIP package, 8 pins
  TM1637_display = IC, SIP package, 4 pins
  BTN_A = Pushbutton [package="[THT]"]
  BTN_B = Pushbutton [package="[THT]"]
  BTN_C = Pushbutton [package="[THT]"]
  part_4 = Resistor [tolerance=±5% resistance=10k package=THT]
  part_5 = Resistor [tolerance=±5% resistance=10k package=THT]
  part_6 = Resistor [tolerance=±5% resistance=10k package=THT]
  part_7 = Rectifier Diode [package="300 mil [THT]"]
  DS18B20_sensor = IC, SIP package, 3 pins
  BC639_transistor = NPN-Transistor [package="TO92 [THT]"]
  part_8 = Rectifier Diode [package="300 mil [THT]"]
  part_9 = Rectifier Diode [package="300 mil [THT]"]
  part_10 = Rectifier Diode [package="300 mil [THT]"]
  part_11 = Resistor [tolerance=±5% resistance=100k package=THT]
  part_12 = Resistor [tolerance=±5% resistance=4.7k package=THT]
  part_13 = Rectifier Diode [package="300 mil [THT]"]
  part_14 = Resistor [tolerance=±5% resistance=1k package=THT]
  part_15 = Ceramic Capacitor [capacitance=220pF package="100 mil [THT, multilayer]"]

nets:
  GND: step_down_converter.pin1, arduino_nano.GND, part_3.Pin_0, MCP2003B.pin5, TM1637_display.pin1, part_4.Pin_0, part_5.Pin_0, part_6.Pin_0, DS18B20_sensor.pin1, DS18B20_sensor.pin3, BC639_transistor.E, part_15.1
  12V: step_down_converter.pin2, arduino_nano.VIN, part_7.anode
  25-35V (pin 1 - red): step_down_converter.pin3
  ground (pin 2 - white): step_down_converter.pin4
  N1: arduino_nano.D1/TX, MCP2003B.pin4
  N2: arduino_nano.D0/RX, part.Pin_1, MCP2003B.pin1
  N3: arduino_nano.D2, BC639_transistor.C
  N4: arduino_nano.D4, TM1637_display.pin3
  N5: arduino_nano.D5, TM1637_display.pin4
  N6: arduino_nano.D6, BTN_A.Pin_1, BTN_A.Pin_2, part_4.Pin_1, part_10.anode
  N7: arduino_nano.D7, BTN_B.Pin_1, BTN_B.Pin_2, part_5.Pin_1, part_8.anode
  N8: arduino_nano.D8, BTN_C.Pin_1, BTN_C.Pin_2, part_6.Pin_1, part_9.anode
  N9: arduino_nano.D9, DS18B20_sensor.pin2, part_12.Pin_0
  5V: arduino_nano.5V, part.Pin_0, part_2.Pin_0, TM1637_display.pin2, BTN_A.Pin_3, BTN_B.Pin_3, BTN_B.Pin_4, BTN_C.Pin_3, part_12.Pin_1
  N10: part_2.Pin_1, MCP2003B.pin2
  N11: part_3.Pin_1, MCP2003B.pin3
  LIN bus (pin 3 - blue): MCP2003B.pin6, part_14.Pin_1, part_15.0
  N12: MCP2003B.pin7, part_7.cathode, part_13.anode
  N13: BC639_transistor.B, part_11.Pin_0
  N14: part_8.cathode, part_9.cathode, part_10.cathode, part_11.Pin_1
  N15: part_13.cathode, part_14.Pin_0
